// Logisim project project.circ as structural Verilog
module main (
  output [31:0] INSTRUCTION,
  output [7:0] out_2
);

  wire clock_1_out, RESET_out;

  Clock clock_1 (.out(clock_1_out));
  Button RESET (.out(RESET_out));
  ROM #(.dataWidth(32)) rom_1 (.addr(out_2), .data(INSTRUCTION));
  PC pc_1 (.clk(clock_1_out), .reset(RESET_out), .out_3(out_2));

  // Notes on the sheet:
  //   contents of rom_1 (hex, n*v repeats v):
  //   100000 1000
endmodule

module PC (
  input  clk,
  input  reset,
  output [7:0] out_3
);

  wire [31:0] adder_1_out, register_1_q;

  Adder #(.width(32)) adder_1 (
    .a(32'h4), .b({register_1_q[31:10], out_3, register_1_q[1:0]}), .out(adder_1_out));  // open: cin, cout
  Register #(.width(32)) register_1 (
    .D(adder_1_out), .clk(clk), .Q({register_1_q[31:10], out_3, register_1_q[1:0]}), .clr(reset));  // open: en
endmodule

// MUXREG1
module BancoDeRegistradores (
  input  [2:0] in_1,
  input  clk,
  input  [7:0] RD1,
  input  [3:0] RW1,
  input  [7:0] WR,
  input  [7:0] RD2,
  input  [3:0] RW2,
  input  [2:0] R2
);

  wire [31:0] MUXREG0, MUXREG1, MUXREG2, MUXREG3;

  Register #(.width(32)) REG0 (.Q(MUXREG0));  // open: D, en, clk, clr
  Register #(.width(32)) REG1 (.Q(MUXREG1));  // open: D, en, clk, clr
  Register #(.width(32)) REG2 (.Q(MUXREG2));  // open: D, en, clk, clr
  Register #(.width(32)) REG3 (.Q(MUXREG3));  // open: D, en, clk, clr
  Register #(.width(32)) REG4 ();  // open: D, en, clk, Q, clr
  Register #(.width(32)) REG5 ();  // open: D, en, clk, Q, clr
  Register #(.width(32)) REG6 ();  // open: D, en, clk, Q, clr
  Register #(.width(32)) REG7 ();  // open: D, en, clk, Q, clr
  Demultiplexer #(.select(3), .width(8)) demultiplexer_1 ();  // open: out0, out1, out2, out3, out4, out5, out6, out7, in, sel
  Multiplexer #(.select(2), .width(32)) multiplexer_1 (
    .in0(MUXREG0), .in1(MUXREG1), .in2(MUXREG2), .in3(MUXREG3));  // open: out, sel
  Multiplexer #(.select(3), .width(8)) multiplexer_2 ();  // open: in0, in1, in2, in3, in4, in5, in6, in7, out, sel
endmodule
